// Logisim project alu.circ as structural Verilog: 18 circuits, main circuit alu
module alu (
  input  [31:0] A,
  input  [31:0] B,
  input  [3:0] ALUSel,
  output [31:0] Result
);

  wire [31:0] add0, and0, bsel_out, mul0, mulh_out, mulhu_out, or0, sll_out, slt_out, sra_out, srl_out, sub0,
       xor0;

  Multiplexer #(.enable("false"), .select(4), .width(32)) multiplexer_1 (
    .in0(add0), .in1(and0), .in2(or0), .in3(xor0), .in4(srl_out), .in5(sra_out), .in6(sll_out),
    .in7(slt_out), .in10(mul0), .in11(mulhu_out), .in12(sub0), .in13(bsel_out), .in14(mulh_out),
    .out(Result), .sel(ALUSel));  // open: in8, in9, in15
  Adder #(.width(32)) adder_1 (.a(A), .b(B), .out(add0));  // open: cin, cout
  assign and0 = A & B;  // AND_Gate and_1, 32 bits wide
  assign or0 = A | B;  // OR_Gate or_1, 32 bits wide
  assign xor0 = A ^ B;  // XOR_Gate xor_1, 32 bits wide
  Subtractor #(.width(32)) subtractor_1 (.a(A), .b(B), .out(sub0));  // open: bin, bout
  Multiplier #(.mode("twosComplement"), .width(32)) multiplier_1 (.a(A), .b(B), .out(mul0));  // open: cin, cout
  srl0 srl0_1 (.A(A), .B(B), .Out1(srl_out));
  sra0 sra0_1 (.A(A), .B(B), .Out1(sra_out));
  sll0 sll0_1 (.A(A), .B(B), .Out1(sll_out));
  slt0 slt0_1 (.A(A), .B(B), .Output1(slt_out));
  bsel0 bsel0_1 (.A(A), .B(B), .Output1(bsel_out));
  mulh0 mulh0_1 (.A(A), .B(B), .Output1(mulh_out));
  mulhu0 mulhu0_1 (.A(A), .B(B), .Output1(mulhu_out));

  // Notes on the sheet:
  //   INPUTS to your circuit
  //   DON'T CHANGE THE LOCATIONS OF THE INPUTS AND OUTPUTS!
  //   OUTPUT from your circuit
endmodule

module sr1 (
  input  in_1,
  input  [31:0] in_2,
  output [31:0] out_3
);

  assign out_3 = {{1{in_1}}, in_2[31:1]};  // Bit_Extender bit_extender_1
endmodule

module sr2 (
  input  in_1,
  input  [31:0] in_2,
  output [31:0] out_3
);

  wire [31:0] sr1_1_out_3;

  sr1 sr1_1 (.in_1(in_1), .in_2(in_2), .out_3(sr1_1_out_3));
  sr1 sr1_2 (.in_1(in_1), .in_2(sr1_1_out_3), .out_3(out_3));
endmodule

module sr4 (
  input  in_1,
  input  [31:0] in_2,
  output [31:0] out_3
);

  wire [31:0] sr2_1_out_3;

  sr2 sr2_1 (.in_1(in_1), .in_2(in_2), .out_3(sr2_1_out_3));
  sr2 sr2_2 (.in_1(in_1), .in_2(sr2_1_out_3), .out_3(out_3));
endmodule

module sr8 (
  input  in_1,
  input  [31:0] in_2,
  output [31:0] out_3
);

  wire [31:0] sr4_1_out_3;

  sr4 sr4_1 (.in_1(in_1), .in_2(in_2), .out_3(sr4_1_out_3));
  sr4 sr4_2 (.in_1(in_1), .in_2(sr4_1_out_3), .out_3(out_3));
endmodule

module sr16 (
  input  in_1,
  input  [31:0] in_2,
  output [31:0] out_3
);

  wire [31:0] sr8_1_out_3;

  sr8 sr8_1 (.in_1(in_1), .in_2(in_2), .out_3(sr8_1_out_3));
  sr8 sr8_2 (.in_1(in_1), .in_2(sr8_1_out_3), .out_3(out_3));
endmodule

module srl0 (
  input  [31:0] A,
  input  [31:0] B,
  output [31:0] Out1
);

  wire [31:0] multiplexer_1_out, multiplexer_2_out, multiplexer_3_out, multiplexer_4_out, sr1_1_out_3,
       sr2_1_out_3, sr4_1_out_3, sr8_1_out_3, sr16_1_out_3;

  // Probe on B[4:0]
  sr1 sr1_1 (.in_1(1'b0), .in_2(A), .out_3(sr1_1_out_3));
  Multiplexer #(.enable("false"), .width(32)) multiplexer_1 (
    .in0(A), .in1(sr1_1_out_3), .out(multiplexer_1_out), .sel(B[0]));
  sr2 sr2_1 (.in_1(1'b0), .in_2(multiplexer_1_out), .out_3(sr2_1_out_3));
  Multiplexer #(.enable("false"), .width(32)) multiplexer_2 (
    .in0(multiplexer_1_out), .in1(sr2_1_out_3), .out(multiplexer_2_out), .sel(B[1]));
  sr4 sr4_1 (.in_1(1'b0), .in_2(multiplexer_2_out), .out_3(sr4_1_out_3));
  Multiplexer #(.enable("false"), .width(32)) multiplexer_3 (
    .in0(multiplexer_2_out), .in1(sr4_1_out_3), .out(multiplexer_3_out), .sel(B[2]));
  sr8 sr8_1 (.in_1(1'b0), .in_2(multiplexer_3_out), .out_3(sr8_1_out_3));
  Multiplexer #(.enable("false"), .width(32)) multiplexer_4 (
    .in0(multiplexer_3_out), .in1(sr8_1_out_3), .out(multiplexer_4_out), .sel(B[3]));
  sr16 sr16_1 (.in_1(1'b0), .in_2(multiplexer_4_out), .out_3(sr16_1_out_3));
  Multiplexer #(.enable("false"), .width(32)) multiplexer_5 (
    .in0(multiplexer_4_out), .in1(sr16_1_out_3), .out(Out1), .sel(B[4]));
endmodule

module sra0 (
  input  [31:0] A,
  input  [31:0] B,
  output [31:0] Out1
);

  wire [31:0] multiplexer_1_out, multiplexer_2_out, multiplexer_3_out, multiplexer_4_out, sr1_1_out_3,
       sr2_1_out_3, sr4_1_out_3, sr8_1_out_3, sr16_1_out_3;

  // Probe on B[4:0]
  sr1 sr1_1 (.in_1(A[31]), .in_2(A), .out_3(sr1_1_out_3));
  Multiplexer #(.enable("false"), .width(32)) multiplexer_1 (
    .in0(A), .in1(sr1_1_out_3), .out(multiplexer_1_out), .sel(B[0]));
  sr2 sr2_1 (.in_1(A[31]), .in_2(multiplexer_1_out), .out_3(sr2_1_out_3));
  Multiplexer #(.enable("false"), .width(32)) multiplexer_2 (
    .in0(multiplexer_1_out), .in1(sr2_1_out_3), .out(multiplexer_2_out), .sel(B[1]));
  sr4 sr4_1 (.in_1(A[31]), .in_2(multiplexer_2_out), .out_3(sr4_1_out_3));
  Multiplexer #(.enable("false"), .width(32)) multiplexer_3 (
    .in0(multiplexer_2_out), .in1(sr4_1_out_3), .out(multiplexer_3_out), .sel(B[2]));
  sr8 sr8_1 (.in_1(A[31]), .in_2(multiplexer_3_out), .out_3(sr8_1_out_3));
  Multiplexer #(.enable("false"), .width(32)) multiplexer_4 (
    .in0(multiplexer_3_out), .in1(sr8_1_out_3), .out(multiplexer_4_out), .sel(B[3]));
  sr16 sr16_1 (.in_1(A[31]), .in_2(multiplexer_4_out), .out_3(sr16_1_out_3));
  Multiplexer #(.enable("false"), .width(32)) multiplexer_5 (
    .in0(multiplexer_4_out), .in1(sr16_1_out_3), .out(Out1), .sel(B[4]));
endmodule

module sl1 (
  input  [31:0] in_1,
  output [31:0] out_2
);


  assign out_2 = {in_1[30:0], 1'b0};
endmodule

module sl2 (
  input  [31:0] in_1,
  output [31:0] out_2
);

  wire [31:0] sl1_1_out_2;

  sl1 sl1_1 (.in_1(in_1), .out_2(sl1_1_out_2));
  sl1 sl1_2 (.in_1(sl1_1_out_2), .out_2(out_2));
endmodule

module sl4 (
  input  [31:0] in_1,
  output [31:0] out_2
);

  wire [31:0] sl2_1_out_2;

  sl2 sl2_1 (.in_1(in_1), .out_2(sl2_1_out_2));
  sl2 sl2_2 (.in_1(sl2_1_out_2), .out_2(out_2));
endmodule

module sl8 (
  input  [31:0] in_1,
  output [31:0] out_2
);

  wire [31:0] sl4_1_out_2;

  sl4 sl4_1 (.in_1(in_1), .out_2(sl4_1_out_2));
  sl4 sl4_2 (.in_1(sl4_1_out_2), .out_2(out_2));
endmodule

module sl16 (
  input  [31:0] in_1,
  output [31:0] out_2
);

  wire [31:0] sl8_1_out_2;

  sl8 sl8_1 (.in_1(in_1), .out_2(sl8_1_out_2));
  sl8 sl8_2 (.in_1(sl8_1_out_2), .out_2(out_2));
endmodule

module sll0 (
  input  [31:0] A,
  input  [31:0] B,
  output [31:0] Out1
);

  wire [31:0] multiplexer_1_out, multiplexer_2_out, multiplexer_3_out, multiplexer_4_out, sl1_1_out_2,
       sl2_1_out_2, sl4_1_out_2, sl8_1_out_2, sl16_1_out_2;

  // Probe on B[4:0]
  sl1 sl1_1 (.in_1(A), .out_2(sl1_1_out_2));
  Multiplexer #(.enable("false"), .width(32)) multiplexer_1 (
    .in0(A), .in1(sl1_1_out_2), .out(multiplexer_1_out), .sel(B[0]));
  sl2 sl2_1 (.in_1(multiplexer_1_out), .out_2(sl2_1_out_2));
  Multiplexer #(.enable("false"), .width(32)) multiplexer_2 (
    .in0(multiplexer_1_out), .in1(sl2_1_out_2), .out(multiplexer_2_out), .sel(B[1]));
  sl4 sl4_1 (.in_1(multiplexer_2_out), .out_2(sl4_1_out_2));
  Multiplexer #(.enable("false"), .width(32)) multiplexer_3 (
    .in0(multiplexer_2_out), .in1(sl4_1_out_2), .out(multiplexer_3_out), .sel(B[2]));
  sl8 sl8_1 (.in_1(multiplexer_3_out), .out_2(sl8_1_out_2));
  Multiplexer #(.enable("false"), .width(32)) multiplexer_4 (
    .in0(multiplexer_3_out), .in1(sl8_1_out_2), .out(multiplexer_4_out), .sel(B[3]));
  sl16 sl16_1 (.in_1(multiplexer_4_out), .out_2(sl16_1_out_2));
  Multiplexer #(.enable("false"), .width(32)) multiplexer_5 (
    .in0(multiplexer_4_out), .in1(sl16_1_out_2), .out(Out1), .sel(B[4]));
endmodule

module slt0 (
  input  [31:0] A,
  input  [31:0] B,
  output [31:0] Output1
);

  wire and_1_out, not_1_out, or_1_out, subtractor_1_bout;
  wire [31:0] subtractor_1_out;

  // Probe on subtractor_1_bout
  Subtractor #(.width(32)) subtractor_1 (.a(A), .b(B), .out(subtractor_1_out), .bout(subtractor_1_bout));  // open: bin
  not not_1 (not_1_out, B[31]);
  and and_1 (and_1_out, A[31], not_1_out);
  or or_1 (or_1_out, and_1_out, subtractor_1_out[31]);
  assign Output1 = {{31{1'b0}}, or_1_out};  // Bit_Extender bit_extender_1
endmodule

module bsel0 (
  input  [31:0] A,
  input  [31:0] B,
  output [31:0] Output1
);

  Multiplexer #(.enable("false"), .width(32)) multiplexer_1 (.in0(A), .in1(B), .out(Output1), .sel(1'b1));
endmodule

module mulh0 (
  input  [31:0] A,
  input  [31:0] B,
  output [31:0] Output1
);

  Multiplier #(.mode("twosComplement"), .width(32)) multiplier_1 (.a(A), .b(B), .cout(Output1));  // open: out, cin
endmodule

module mulhu0 (
  input  [31:0] A,
  input  [31:0] B,
  output [31:0] Output1
);

  Multiplier #(.width(32)) multiplier_1 (.a(A), .b(B), .cout(Output1));  // open: out, cin
endmodule
