// Logisim project control_logic.circ as structural Verilog: 12 circuits, main circuit control_logic
module control_logic (
  input  [31:0] inst,
  input  BrEq,
  input  BrLt,
  output PCSel,
  output RegWEn,
  output [2:0] ImmSel,
  output BrUn,
  output ASel,
  output BSel,
  output [3:0] ALUSel,
  output MemRW,
  output [1:0] WBSel,
  output CSRSel,
  output CSRWen,
  output [3:0] WRITE_ENABLE,
  output [3:0] LOAD_ENABLE
);

  PCSel0 pcsel0_1 (.BrEq(BrEq), .opcode(inst[6:2]), .BrLt(BrLt), .funct3(inst[14:12]), .PCSel_Output(PCSel));
  ImmSel0 immsel0_1 (.opcode(inst[6:2]), .funct7(inst[31:25]), .funct3(inst[14:12]), .ImmSel_Output(ImmSel));
  ASel0 asel0_1 (.opcode(inst[6:2]), .ASEL_Output(ASel));
  ALUSel0 alusel0_1 (.opcode(inst[6:2]), .funct7(inst[31:25]), .funct3(inst[14:12]), .ALUSel_Output(ALUSel));
  WBSel0 wbsel0_1 (.opcode(inst[6:2]), .funct7(inst[31:25]), .funct3(inst[14:12]), .WBSel_Output(WBSel));
  CSRWen0 csrwen0_1 (.opcode(inst[6:2]), .funct3(inst[14:12]), .CSRWen_output(CSRWen));
  RegWEn0 regwen0_1 (.opcode(inst[6:2]), .RegWEn_Output(RegWEn));
  BrUn0 brun0_1 (.opcode(inst[6:2]), .funct3(inst[14:12]), .BrUn_Output(BrUn));
  BSel0 bsel0_1 (.opcode(inst[6:2]), .funct7(inst[31:25]), .funct3(inst[14:12]), .BSel_Output(BSel));
  MemRW0 memrw0_1 (
    .funct3(inst[14:12]), .opcode(inst[6:2]), .MemRW_Output(MemRW), .WRITE_ENABLE(WRITE_ENABLE),
    .LOAD_ENABLE(LOAD_ENABLE));
  CSRSel0 csrsel0_1 (.opcode(inst[6:2]), .funct3(inst[14:12]), .CSRRWI(CSRSel));

  // Other names for the same wires on the sheet: opcode[4:0] = inst[6:2]; funct3[2:0] = inst[14:12];
  //   funct7[6:0] = inst[31:25]

  // Notes on the sheet:
  //   INPUTS to your circuit
  //   DON'T CHANGE THE LOCATIONS OF THE INPUTS AND OUTPUTS!
  //   OUTPUT from your circuit
endmodule

module ASel0 (
  input  [4:0] opcode,
  output ASEL_Output
);

  wire AND0_out, AND1_out, AND2_out, not_1_out, not_2_out, not_3_out, not_4_out, not_5_out, not_6_out,
       not_7_out;

  not not_1 (not_1_out, opcode[0]);
  not not_2 (not_2_out, opcode[1]);
  not not_3 (not_3_out, opcode[2]);
  not not_4 (not_4_out, opcode[1]);
  not not_5 (not_5_out, opcode[3]);
  not not_6 (not_6_out, opcode[4]);
  not not_7 (not_7_out, opcode[2]);
  and AND0 (AND0_out, not_1_out, not_2_out, not_3_out, opcode[3], opcode[4]);
  and AND1 (AND1_out, opcode[0], not_4_out, opcode[2], not_5_out, not_6_out);
  // Probe on AND1_out
  and AND2 (AND2_out, opcode[0], opcode[1], not_7_out, opcode[3], opcode[4]);
  or or_1 (ASEL_Output, AND0_out, AND1_out, AND2_out);

  // Other names for the same wires on the sheet: A0 = opcode[0]; A1 = opcode[1]; A2 = opcode[2]; A3 = opcode[3];
  //   A4 = opcode[4]
endmodule

module PCSel0 (
  input  BrEq,
  input  [4:0] opcode,
  input  BrLt,
  input  [2:0] funct3,
  output PCSel_Output
);

  wire and_6_out, BEQ, BGE, BGEU, BLT, BLTU, BNE, I_JALR, not_1_out, not_2_out, not_3_out, not_4_out,
       not_5_out, not_6_out, not_7_out, not_8_out, not_9_out, not_10_out, not_11_out, not_12_out, not_13_out,
       not_14_out, not_15_out, not_16_out, not_17_out, not_18_out, not_19_out, not_20_out, not_21_out,
       not_22_out, not_23_out, or_1_out, SB, UJ;

  not not_1 (not_1_out, opcode[0]);
  not not_2 (not_2_out, opcode[1]);
  not not_3 (not_3_out, opcode[2]);
  not not_4 (not_4_out, opcode[1]);
  not not_5 (not_5_out, opcode[2]);
  not not_6 (not_6_out, funct3[0]);
  not not_7 (not_7_out, funct3[1]);
  not not_8 (not_8_out, funct3[2]);
  not not_9 (not_9_out, funct3[0]);
  not not_10 (not_10_out, funct3[1]);
  not not_11 (not_11_out, funct3[2]);
  not not_12 (not_12_out, funct3[0]);
  not not_13 (not_13_out, funct3[1]);
  not not_14 (not_14_out, funct3[0]);
  and and_1 (SB, not_1_out, not_2_out, not_3_out, opcode[3], opcode[4]);
  and and_2 (I_JALR, opcode[0], not_4_out, not_5_out, opcode[3], opcode[4], not_6_out, not_7_out, not_8_out);
  and and_3 (BEQ, not_9_out, not_10_out, not_11_out, BrEq);
  and and_4 (BLT, not_12_out, not_13_out, funct3[2], BrLt);
  and and_5 (BLTU, not_14_out, funct3[1], funct3[2], BrLt);
  or or_1 (or_1_out, BEQ, BLT, BLTU, BNE, BGE, BGEU);
  and and_6 (and_6_out, or_1_out, SB);
  not not_15 (not_15_out, opcode[2]);
  not not_16 (not_16_out, funct3[1]);
  not not_17 (not_17_out, funct3[2]);
  not not_18 (not_18_out, BrEq);
  not not_19 (not_19_out, funct3[1]);
  not not_20 (not_20_out, BrEq);
  not not_21 (not_21_out, BrLt);
  not not_22 (not_22_out, BrEq);
  not not_23 (not_23_out, BrLt);
  or or_2 (PCSel_Output, and_6_out, I_JALR, UJ);
  and and_7 (UJ, opcode[0], opcode[1], not_15_out, opcode[3], opcode[4]);
  and and_8 (BNE, funct3[0], not_16_out, not_17_out, not_18_out);
  and and_9 (BGE, funct3[0], not_19_out, funct3[2], not_20_out, not_21_out);
  and and_10 (BGEU, funct3[0], funct3[1], funct3[2], not_22_out, not_23_out);

  // Other names for the same wires on the sheet: B0 = funct3[0]; B1 = funct3[1]; B2 = funct3[2]; A0 = opcode[0];
  //   A1 = opcode[1]; A2 = opcode[2]; A3 = opcode[3]; A4 = opcode[4]
endmodule

module BrUn0 (
  input  [4:0] opcode,
  input  [2:0] funct3,
  output BrUn_Output
);

  wire BGEU, BLTU, not_1_out, not_2_out, not_3_out, not_4_out, or_1_out, SB;

  not not_1 (not_1_out, opcode[0]);
  not not_2 (not_2_out, opcode[1]);
  not not_3 (not_3_out, opcode[2]);
  not not_4 (not_4_out, funct3[0]);
  or or_1 (or_1_out, BLTU, BGEU);
  and and_1 (SB, not_1_out, not_2_out, not_3_out, opcode[3], opcode[4]);
  and and_2 (BLTU, not_4_out, funct3[1], funct3[2]);
  and and_3 (BrUn_Output, SB, or_1_out);
  and and_4 (BGEU, funct3[0], funct3[1], funct3[2]);

  // Other names for the same wires on the sheet: B0 = funct3[0]; B1 = funct3[1]; B2 = funct3[2]; A0 = opcode[0];
  //   A1 = opcode[1]; A2 = opcode[2]; A3 = opcode[3]; A4 = opcode[4]
endmodule

module BSel0 (
  input  [4:0] opcode,
  input  [6:0] funct7,
  input  [2:0] funct3,
  output BSel_Output
);

  wire ADDI, ANDI, BEQ, BGE, BGEU, BLT, BLTU, BNE, I, I_JALR, I_LOAD, LB, LH, LW, not_1_out, not_2_out,
       not_3_out, not_4_out, not_5_out, not_6_out, not_7_out, not_8_out, not_9_out, not_10_out, not_11_out,
       not_12_out, not_13_out, not_14_out, not_15_out, not_16_out, not_17_out, not_18_out, not_19_out,
       not_20_out, not_21_out, not_22_out, not_23_out, not_24_out, not_25_out, not_26_out, not_27_out,
       not_28_out, not_29_out, not_30_out, not_31_out, not_32_out, not_33_out, not_34_out, not_35_out,
       not_36_out, not_37_out, not_38_out, not_39_out, not_40_out, not_41_out, not_42_out, not_43_out,
       not_44_out, not_45_out, not_46_out, not_47_out, not_48_out, not_49_out, not_50_out, not_51_out,
       not_52_out, not_53_out, not_54_out, not_55_out, not_56_out, not_57_out, not_58_out, not_59_out,
       not_60_out, not_61_out, not_62_out, not_63_out, not_64_out, not_65_out, not_66_out, not_67_out,
       not_68_out, not_69_out, not_70_out, not_71_out, not_72_out, not_73_out, not_74_out, not_75_out,
       not_76_out, not_77_out, not_78_out, not_79_out, not_80_out, not_81_out, not_82_out, ORI, S, S_SB, SB,
       SH, SLLI, SLTI, SRAI, SRLI, SW, U_AUIPC, U_LUI, UJ, XORI;

  not not_1 (not_1_out, opcode[0]);
  not not_2 (not_2_out, opcode[1]);
  not not_3 (not_3_out, opcode[2]);
  not not_4 (not_4_out, opcode[3]);
  not not_5 (not_5_out, opcode[4]);
  not not_6 (not_6_out, opcode[0]);
  not not_7 (not_7_out, opcode[1]);
  not not_8 (not_8_out, opcode[2]);
  not not_9 (not_9_out, opcode[1]);
  not not_10 (not_10_out, opcode[3]);
  not not_11 (not_11_out, opcode[4]);
  not not_12 (not_12_out, opcode[1]);
  not not_13 (not_13_out, opcode[2]);
  not not_14 (not_14_out, funct3[0]);
  not not_15 (not_15_out, funct3[1]);
  not not_16 (not_16_out, funct3[2]);
  not not_17 (not_17_out, funct3[0]);
  not not_18 (not_18_out, funct3[1]);
  not not_19 (not_19_out, funct3[2]);
  not not_20 (not_20_out, funct3[0]);
  not not_21 (not_21_out, funct3[1]);
  not not_22 (not_22_out, funct3[0]);
  not not_23 (not_23_out, funct3[0]);
  not not_24 (not_24_out, funct3[1]);
  not not_25 (not_25_out, funct3[2]);
  not not_26 (not_26_out, funct3[1]);
  not not_27 (not_27_out, funct3[2]);
  not not_28 (not_28_out, funct7[0]);
  not not_29 (not_29_out, funct7[1]);
  not not_30 (not_30_out, funct7[2]);
  not not_31 (not_31_out, funct7[3]);
  not not_32 (not_32_out, funct7[4]);
  not not_33 (not_33_out, funct7[5]);
  not not_34 (not_34_out, funct7[6]);
  not not_35 (not_35_out, funct3[0]);
  not not_36 (not_36_out, funct3[2]);
  not not_37 (not_37_out, funct3[0]);
  not not_38 (not_38_out, funct3[1]);
  not not_39 (not_39_out, funct3[0]);
  not not_40 (not_40_out, funct3[1]);
  not not_41 (not_41_out, funct3[2]);
  not not_42 (not_42_out, funct3[0]);
  not not_43 (not_43_out, funct3[2]);
  not not_44 (not_44_out, funct3[0]);
  not not_45 (not_45_out, funct3[1]);
  not not_46 (not_46_out, funct3[2]);
  not not_47 (not_47_out, funct3[0]);
  not not_48 (not_48_out, funct3[2]);
  and and_1 (I_LOAD, not_1_out, not_2_out, not_3_out, not_4_out, not_5_out);
  and and_2 (SB, not_6_out, not_7_out, not_8_out, opcode[3], opcode[4]);
  and and_3 (U_AUIPC, opcode[0], not_9_out, opcode[2], not_10_out, not_11_out);
  and and_4 (I_JALR, opcode[0], not_12_out, not_13_out, opcode[3], opcode[4], not_14_out, not_15_out, not_16_out);
  and and_5 (BEQ, not_17_out, not_18_out, not_19_out, SB);
  and and_6 (BLT, not_20_out, not_21_out, funct3[2], SB);
  and and_7 (BLTU, not_22_out, funct3[1], funct3[2], SB);
  and and_8 (ADDI, not_23_out, not_24_out, not_25_out, I);
  and and_9 (SLLI, funct3[0], not_26_out, not_27_out, not_28_out, not_29_out, not_30_out, not_31_out, not_32_out, not_33_out, not_34_out, I);
  and and_10 (SLTI, not_35_out, funct3[1], not_36_out, I);
  and and_11 (XORI, not_37_out, not_38_out, funct3[2], I);
  and and_12 (ANDI, funct3[0], funct3[1], funct3[2], I);
  and and_13 (LB, not_39_out, not_40_out, not_41_out, I_LOAD);
  and and_14 (LW, not_42_out, funct3[1], not_43_out, I_LOAD);
  and and_15 (S_SB, not_44_out, not_45_out, not_46_out, S);
  and and_16 (SW, not_47_out, funct3[1], not_48_out, S);
  or or_1 (BSel_Output, LB, LH, LW, S_SB, SH, SW, ADDI, SLLI, SLTI, XORI, SRLI, SRAI, ORI, ANDI, BEQ, BLT, BLTU, BNE, BGE, BGEU, U_AUIPC, U_LUI, UJ, I_JALR);
  not not_49 (not_49_out, opcode[0]);
  not not_50 (not_50_out, opcode[1]);
  not not_51 (not_51_out, opcode[3]);
  not not_52 (not_52_out, opcode[4]);
  not not_53 (not_53_out, opcode[0]);
  not not_54 (not_54_out, opcode[1]);
  not not_55 (not_55_out, opcode[2]);
  not not_56 (not_56_out, opcode[4]);
  not not_57 (not_57_out, opcode[1]);
  not not_58 (not_58_out, opcode[4]);
  not not_59 (not_59_out, opcode[2]);
  not not_60 (not_60_out, funct3[1]);
  not not_61 (not_61_out, funct3[2]);
  not not_62 (not_62_out, funct3[1]);
  not not_63 (not_63_out, funct3[1]);
  not not_64 (not_64_out, funct7[0]);
  not not_65 (not_65_out, funct7[1]);
  not not_66 (not_66_out, funct7[2]);
  not not_67 (not_67_out, funct7[3]);
  not not_68 (not_68_out, funct7[4]);
  not not_69 (not_69_out, funct7[5]);
  not not_70 (not_70_out, funct7[6]);
  not not_71 (not_71_out, funct3[1]);
  not not_72 (not_72_out, funct7[0]);
  not not_73 (not_73_out, funct7[1]);
  not not_74 (not_74_out, funct7[2]);
  not not_75 (not_75_out, funct7[3]);
  not not_76 (not_76_out, funct7[4]);
  not not_77 (not_77_out, funct7[6]);
  not not_78 (not_78_out, funct3[0]);
  not not_79 (not_79_out, funct3[1]);
  not not_80 (not_80_out, funct3[2]);
  not not_81 (not_81_out, funct3[1]);
  not not_82 (not_82_out, funct3[2]);
  and and_17 (I, not_49_out, not_50_out, opcode[2], not_51_out, not_52_out);
  and and_18 (S, not_53_out, not_54_out, not_55_out, opcode[3], not_56_out);
  and and_19 (U_LUI, opcode[0], not_57_out, opcode[2], opcode[3], not_58_out);
  and and_20 (UJ, opcode[0], opcode[1], not_59_out, opcode[3], opcode[4]);
  and and_21 (BNE, funct3[0], not_60_out, not_61_out, SB);
  and and_22 (BGE, funct3[0], not_62_out, funct3[2], SB);
  and and_23 (BGEU, funct3[0], funct3[1], funct3[2], SB);
  and and_24 (SRLI, funct3[0], not_63_out, funct3[2], not_64_out, not_65_out, not_66_out, not_67_out, not_68_out, not_69_out, not_70_out, I);
  and and_25 (SRAI, funct3[0], not_71_out, funct3[2], not_72_out, not_73_out, not_74_out, not_75_out, not_76_out, funct7[5], not_77_out, I);
  and and_26 (ORI, not_78_out, funct3[1], funct3[2], I);
  and and_27 (LH, funct3[0], not_79_out, not_80_out, I_LOAD);
  and and_28 (SH, funct3[0], not_81_out, not_82_out, S);

  // Other names for the same wires on the sheet: B0 = funct3[0]; B1 = funct3[1]; B2 = funct3[2]; C0 = funct7[0];
  //   C1 = funct7[1]; C2 = funct7[2]; C3 = funct7[3]; C4 = funct7[4]; C5 = funct7[5]; C6 = funct7[6]; A0 = opcode[0];
  //   A1 = opcode[1]; A2 = opcode[2]; A3 = opcode[3]; A4 = opcode[4]
endmodule

module RegWEn0 (
  input  [4:0] opcode,
  output RegWEn_Output
);

  wire I, I_JALR, I_LOAD, not_1_out, not_2_out, not_3_out, not_4_out, not_5_out, not_6_out, not_7_out,
       not_8_out, not_9_out, not_10_out, not_11_out, not_12_out, not_13_out, not_14_out, not_15_out,
       not_16_out, not_17_out, not_18_out, not_19_out, not_20_out, R, U_AUIPC, U_LUI, UJ;

  not not_1 (not_1_out, opcode[0]);
  not not_2 (not_2_out, opcode[1]);
  not not_3 (not_3_out, opcode[2]);
  not not_4 (not_4_out, opcode[3]);
  not not_5 (not_5_out, opcode[4]);
  not not_6 (not_6_out, opcode[1]);
  not not_7 (not_7_out, opcode[3]);
  not not_8 (not_8_out, opcode[4]);
  not not_9 (not_9_out, opcode[1]);
  not not_10 (not_10_out, opcode[2]);
  not not_11 (not_11_out, opcode[0]);
  not not_12 (not_12_out, opcode[1]);
  not not_13 (not_13_out, opcode[4]);
  and and_1 (I_LOAD, not_1_out, not_2_out, not_3_out, not_4_out, not_5_out);
  and and_2 (R, not_11_out, not_12_out, opcode[2], opcode[3], not_13_out);
  and and_3 (U_AUIPC, opcode[0], not_6_out, opcode[2], not_7_out, not_8_out);
  and and_4 (I_JALR, opcode[0], not_9_out, not_10_out, opcode[3], opcode[4]);
  or or_1 (RegWEn_Output, R, I_LOAD, I, U_AUIPC, U_LUI, I_JALR, UJ);
  not not_14 (not_14_out, opcode[0]);
  not not_15 (not_15_out, opcode[1]);
  not not_16 (not_16_out, opcode[3]);
  not not_17 (not_17_out, opcode[4]);
  not not_18 (not_18_out, opcode[1]);
  not not_19 (not_19_out, opcode[4]);
  not not_20 (not_20_out, opcode[2]);
  and and_5 (I, not_14_out, not_15_out, opcode[2], not_16_out, not_17_out);
  and and_6 (U_LUI, opcode[0], not_18_out, opcode[2], opcode[3], not_19_out);
  and and_7 (UJ, opcode[0], opcode[1], not_20_out, opcode[3], opcode[4]);

  // Other names for the same wires on the sheet: A0 = opcode[0]; A1 = opcode[1]; A2 = opcode[2]; A3 = opcode[3];
  //   A4 = opcode[4]
endmodule

module MemRW0 (
  input  [2:0] funct3,
  input  [4:0] opcode,
  output MemRW_Output,
  output [3:0] WRITE_ENABLE,
  output [3:0] LOAD_ENABLE
);

  wire I_LOAD, LB, LH, LW, not_1_out, not_2_out, not_3_out, not_4_out, not_5_out, not_6_out, not_7_out,
       not_8_out, not_9_out, not_10_out, not_11_out, not_12_out, not_13_out, not_14_out, not_15_out,
       not_16_out, not_17_out, not_18_out, not_19_out, not_20_out, not_21_out, not_22_out, not_23_out, S_SB,
       SH, SW;
  wire [3:0] GROUP1, GROUP3, GROUP15, multiplexer_1_out, multiplexer_2_out, multiplexer_3_out;

  not not_1 (not_1_out, opcode[0]);
  not not_2 (not_2_out, opcode[1]);
  not not_3 (not_3_out, opcode[2]);
  not not_4 (not_4_out, opcode[4]);
  not not_5 (not_5_out, funct3[0]);
  not not_6 (not_6_out, funct3[1]);
  not not_7 (not_7_out, funct3[2]);
  not not_8 (not_8_out, funct3[0]);
  not not_9 (not_9_out, funct3[2]);
  not not_10 (not_10_out, funct3[0]);
  not not_11 (not_11_out, funct3[1]);
  not not_12 (not_12_out, funct3[2]);
  not not_13 (not_13_out, funct3[0]);
  not not_14 (not_14_out, funct3[2]);
  Multiplexer #(.enable("false"), .width(4)) multiplexer_1 (
    .in0(4'b0000), .in1(4'b0001), .out(multiplexer_1_out), .sel(LB));
  Multiplexer #(.enable("false"), .width(4)) multiplexer_2 (
    .in0(4'b0000), .in1(4'b0011), .out(multiplexer_2_out), .sel(LH));
  Multiplexer #(.enable("false"), .width(4)) multiplexer_3 (
    .in0(4'b0000), .in1(4'b1111), .out(multiplexer_3_out), .sel(LW));
  Multiplexer #(.enable("false"), .width(4)) multiplexer_4 (.in0(4'b0000), .in1(4'b0001), .out(GROUP1), .sel(S_SB));
  Multiplexer #(.enable("false"), .width(4)) multiplexer_5 (.in0(4'b0000), .in1(4'b1111), .out(GROUP15), .sel(SW));
  and and_1 (MemRW_Output, not_1_out, not_2_out, not_3_out, opcode[3], not_4_out);
  and and_2 (S_SB, not_5_out, not_6_out, not_7_out, MemRW_Output);
  and and_3 (SW, not_8_out, funct3[1], not_9_out, MemRW_Output);
  assign WRITE_ENABLE = GROUP1 | GROUP3 | GROUP15;  // OR_Gate or_1, 4 bits wide
  and and_4 (LB, not_10_out, not_11_out, not_12_out, I_LOAD);
  and and_5 (LW, not_13_out, funct3[1], not_14_out, I_LOAD);
  assign LOAD_ENABLE = multiplexer_1_out | multiplexer_2_out | multiplexer_3_out;  // OR_Gate or_2, 4 bits wide
  not not_15 (not_15_out, funct3[1]);
  not not_16 (not_16_out, funct3[2]);
  Multiplexer #(.enable("false"), .width(4)) multiplexer_6 (.in0(4'b0000), .in1(4'b0011), .out(GROUP3), .sel(SH));
  not not_17 (not_17_out, funct3[1]);
  not not_18 (not_18_out, funct3[2]);
  not not_19 (not_19_out, opcode[0]);
  not not_20 (not_20_out, opcode[1]);
  not not_21 (not_21_out, opcode[2]);
  not not_22 (not_22_out, opcode[3]);
  not not_23 (not_23_out, opcode[4]);
  and and_6 (SH, funct3[0], not_15_out, not_16_out, MemRW_Output);
  and and_7 (LH, funct3[0], not_17_out, not_18_out, I_LOAD);
  and and_8 (I_LOAD, not_19_out, not_20_out, not_21_out, not_22_out, not_23_out);

  // Other names for the same wires on the sheet: B0 = funct3[0]; B1 = funct3[1]; B2 = funct3[2]; A0 = opcode[0];
  //   A1 = opcode[1]; A2 = opcode[2]; A3 = opcode[3]; A4 = opcode[4]; S = MemRW_Output
endmodule

module CSRSel0 (
  input  [4:0] opcode,
  input  [2:0] funct3,
  output CSRRWI
);

  wire CSR, not_1_out, not_2_out, not_3_out;

  not not_1 (not_1_out, opcode[0]);
  not not_2 (not_2_out, opcode[1]);
  not not_3 (not_3_out, funct3[1]);
  and and_1 (CSR, not_1_out, not_2_out, opcode[2], opcode[3], opcode[4]);
  and and_2 (CSRRWI, CSR, funct3[0], not_3_out, funct3[2]);

  // Other names for the same wires on the sheet: B0 = funct3[0]; B1 = funct3[1]; B2 = funct3[2]; A0 = opcode[0];
  //   A1 = opcode[1]; A2 = opcode[2]; A3 = opcode[3]; A4 = opcode[4]
endmodule

module CSRWen0 (
  input  [4:0] opcode,
  input  [2:0] funct3,
  output CSRWen_output
);

  wire CSR, CSRRW, CSRRWI, not_1_out, not_2_out, not_3_out, not_4_out, not_5_out;

  not not_1 (not_1_out, funct3[1]);
  not not_2 (not_2_out, funct3[2]);
  not not_3 (not_3_out, funct3[1]);
  not not_4 (not_4_out, opcode[0]);
  not not_5 (not_5_out, opcode[1]);
  and and_1 (CSRRW, CSR, funct3[0], not_1_out, not_2_out);
  and and_2 (CSRRWI, CSR, funct3[0], not_3_out, funct3[2]);
  and and_3 (CSR, not_4_out, not_5_out, opcode[2], opcode[3], opcode[4]);
  or or_1 (CSRWen_output, CSRRW, CSRRWI);

  // Other names for the same wires on the sheet: B0 = funct3[0]; B1 = funct3[1]; B2 = funct3[2]; A0 = opcode[0];
  //   A1 = opcode[1]; A2 = opcode[2]; A3 = opcode[3]; A4 = opcode[4]
endmodule

module ALUSel0 (
  input  [4:0] opcode,
  input  [6:0] funct7,
  input  [2:0] funct3,
  output [3:0] ALUSel_Output
);

  wire ADD, ADDI, AND0, ANDI, I, MUL, MULH, MULHU, not_1_out, not_2_out, not_3_out, not_4_out, not_5_out,
       not_6_out, not_7_out, not_8_out, not_9_out, not_10_out, not_11_out, not_12_out, not_13_out,
       not_14_out, not_15_out, not_16_out, not_17_out, not_18_out, not_19_out, not_20_out, not_21_out,
       not_22_out, not_23_out, not_24_out, not_25_out, not_26_out, not_27_out, not_28_out, not_29_out,
       not_30_out, not_31_out, not_32_out, not_33_out, not_34_out, not_35_out, not_36_out, not_37_out,
       not_38_out, not_39_out, not_40_out, not_41_out, not_42_out, not_43_out, not_44_out, not_45_out,
       not_46_out, not_47_out, not_48_out, not_49_out, not_50_out, not_51_out, not_52_out, not_53_out,
       not_54_out, not_55_out, not_56_out, not_57_out, not_58_out, not_59_out, not_60_out, not_61_out,
       not_62_out, not_63_out, not_64_out, not_65_out, not_66_out, not_67_out, not_68_out, not_69_out,
       not_70_out, not_71_out, not_72_out, not_73_out, not_74_out, not_75_out, not_76_out, not_77_out,
       not_78_out, not_79_out, not_80_out, not_81_out, not_82_out, not_83_out, not_84_out, not_85_out,
       not_86_out, not_87_out, not_88_out, not_89_out, not_90_out, not_91_out, not_92_out, not_93_out,
       not_94_out, not_95_out, not_96_out, not_97_out, not_98_out, not_99_out, not_100_out, not_101_out,
       not_102_out, not_103_out, not_104_out, not_105_out, not_106_out, not_107_out, not_108_out,
       not_109_out, not_110_out, not_111_out, not_112_out, not_113_out, not_114_out, not_115_out,
       not_116_out, not_117_out, not_118_out, not_119_out, not_120_out, not_121_out, not_122_out,
       not_123_out, not_124_out, not_125_out, not_126_out, not_127_out, not_128_out, not_129_out,
       not_130_out, not_131_out, not_132_out, not_133_out, not_134_out, not_135_out, not_136_out,
       not_137_out, not_138_out, not_139_out, OR0, or_1_out, or_2_out, or_3_out, or_4_out, or_6_out,
       or_7_out, or_8_out, or_9_out, ORI, R, SLL0, SLLI, SLT, SLTI, SRA0, SRAI, SRL0, SRLI, SUB, XOR0, XORI;
  wire [3:0] ADD_GROUP, AND_GROUP, MUL_GROUP, MULH_GROUP, MULHU_GROUP, OR_GROUP, SLL_GROUP, SLT_GROUP,
       SRA_GROUP, SRL_GROUP, SUB_GROUP, XOR_GROUP;

  not not_1 (not_1_out, opcode[0]);
  not not_2 (not_2_out, opcode[1]);
  not not_3 (not_3_out, opcode[4]);
  not not_4 (not_4_out, funct3[0]);
  not not_5 (not_5_out, funct3[1]);
  not not_6 (not_6_out, funct3[2]);
  not not_7 (not_7_out, funct3[1]);
  not not_8 (not_8_out, funct3[2]);
  not not_9 (not_9_out, funct7[0]);
  not not_10 (not_10_out, funct7[1]);
  not not_11 (not_11_out, funct7[2]);
  not not_12 (not_12_out, funct7[3]);
  not not_13 (not_13_out, funct7[4]);
  not not_14 (not_14_out, funct7[5]);
  not not_15 (not_15_out, funct7[6]);
  not not_16 (not_16_out, funct3[0]);
  not not_17 (not_17_out, funct3[2]);
  not not_18 (not_18_out, funct3[0]);
  not not_19 (not_19_out, funct3[1]);
  not not_20 (not_20_out, funct3[0]);
  not not_21 (not_21_out, funct3[1]);
  not not_22 (not_22_out, funct3[2]);
  not not_23 (not_23_out, funct7[0]);
  not not_24 (not_24_out, funct7[1]);
  not not_25 (not_25_out, funct7[2]);
  not not_26 (not_26_out, funct7[3]);
  not not_27 (not_27_out, funct7[4]);
  not not_28 (not_28_out, funct7[5]);
  not not_29 (not_29_out, funct7[6]);
  not not_30 (not_30_out, funct3[0]);
  not not_31 (not_31_out, funct3[1]);
  not not_32 (not_32_out, funct3[2]);
  not not_33 (not_33_out, funct7[0]);
  not not_34 (not_34_out, funct7[1]);
  not not_35 (not_35_out, funct7[2]);
  not not_36 (not_36_out, funct7[3]);
  not not_37 (not_37_out, funct7[4]);
  not not_38 (not_38_out, funct7[6]);
  not not_39 (not_39_out, funct3[1]);
  not not_40 (not_40_out, funct3[2]);
  not not_41 (not_41_out, funct7[1]);
  not not_42 (not_42_out, funct7[2]);
  not not_43 (not_43_out, funct7[3]);
  not not_44 (not_44_out, funct7[4]);
  not not_45 (not_45_out, funct7[5]);
  not not_46 (not_46_out, funct7[6]);
  not not_47 (not_47_out, funct3[0]);
  not not_48 (not_48_out, funct3[2]);
  not not_49 (not_49_out, funct7[0]);
  not not_50 (not_50_out, funct7[1]);
  not not_51 (not_51_out, funct7[2]);
  not not_52 (not_52_out, funct7[3]);
  not not_53 (not_53_out, funct7[4]);
  not not_54 (not_54_out, funct7[5]);
  not not_55 (not_55_out, funct7[6]);
  not not_56 (not_56_out, funct3[1]);
  not not_57 (not_57_out, funct7[0]);
  not not_58 (not_58_out, funct7[1]);
  not not_59 (not_59_out, funct7[2]);
  not not_60 (not_60_out, funct7[3]);
  not not_61 (not_61_out, funct7[4]);
  not not_62 (not_62_out, funct7[5]);
  not not_63 (not_63_out, funct7[6]);
  not not_64 (not_64_out, funct3[0]);
  not not_65 (not_65_out, funct7[0]);
  not not_66 (not_66_out, funct7[1]);
  not not_67 (not_67_out, funct7[2]);
  not not_68 (not_68_out, funct7[3]);
  not not_69 (not_69_out, funct7[4]);
  not not_70 (not_70_out, funct7[5]);
  not not_71 (not_71_out, funct7[6]);
  or or_1 (or_1_out, ADD, ADDI);
  or or_2 (or_2_out, SLT, SLTI);
  or or_3 (or_3_out, SRA0, SRAI);
  or or_4 (or_4_out, AND0, ANDI);
  Multiplexer #(.enable("false"), .width(4)) multiplexer_1 (
    .in0(4'b0000), .in1(4'b0000), .out(ADD_GROUP), .sel(or_1_out));
  Multiplexer #(.enable("false"), .width(4)) multiplexer_2 (.in0(4'b0000), .in1(4'b1100), .out(SUB_GROUP), .sel(SUB));
  Multiplexer #(.enable("false"), .width(4)) multiplexer_3 (.in0(4'b0000), .in1(4'b1110), .out(MULH_GROUP), .sel(MULH));
  Multiplexer #(.enable("false"), .width(4)) multiplexer_4 (
    .in0(4'b0000), .in1(4'b0111), .out(SLT_GROUP), .sel(or_2_out));
  Multiplexer #(.enable("false"), .width(4)) multiplexer_5 (
    .in0(4'b0000), .in1(4'b0101), .out(SRA_GROUP), .sel(or_3_out));
  Multiplexer #(.enable("false"), .width(4)) multiplexer_6 (
    .in0(4'b0000), .in1(4'b0001), .out(AND_GROUP), .sel(or_4_out));
  and and_1 (R, not_1_out, not_2_out, opcode[2], opcode[3], not_3_out);
  and and_2 (ADDI, not_4_out, not_5_out, not_6_out, I);
  and and_3 (SLLI, funct3[0], not_7_out, not_8_out, not_9_out, not_10_out, not_11_out, not_12_out, not_13_out, not_14_out, not_15_out, I);
  and and_4 (SLTI, not_16_out, funct3[1], not_17_out, I);
  and and_5 (XORI, not_18_out, not_19_out, funct3[2], I);
  and and_6 (ANDI, funct3[0], funct3[1], funct3[2], I);
  and and_7 (ADD, not_20_out, not_21_out, not_22_out, not_23_out, not_24_out, not_25_out, not_26_out, not_27_out, not_28_out, not_29_out, R);
  and and_8 (SUB, not_30_out, not_31_out, not_32_out, not_33_out, not_34_out, not_35_out, not_36_out, not_37_out, funct7[5], not_38_out, R);
  and and_9 (MULH, funct3[0], not_39_out, not_40_out, funct7[0], not_41_out, not_42_out, not_43_out, not_44_out, not_45_out, not_46_out, R);
  and and_10 (SLT, not_47_out, funct3[1], not_48_out, not_49_out, not_50_out, not_51_out, not_52_out, not_53_out, not_54_out, not_55_out, R);
  and and_11 (SRL0, funct3[0], not_56_out, funct3[2], not_57_out, not_58_out, not_59_out, not_60_out, not_61_out, not_62_out, not_63_out, R);
  and and_12 (OR0, not_64_out, funct3[1], funct3[2], not_65_out, not_66_out, not_67_out, not_68_out, not_69_out, not_70_out, not_71_out, R);
  assign ALUSel_Output = ADD_GROUP | SUB_GROUP | MULH_GROUP | SLT_GROUP | SRA_GROUP | AND_GROUP | MUL_GROUP | SLL_GROUP | MULHU_GROUP | SRL_GROUP | XOR_GROUP | OR_GROUP;  // OR_Gate or_5, 4 bits wide
  not not_72 (not_72_out, funct3[1]);
  not not_73 (not_73_out, funct7[0]);
  not not_74 (not_74_out, funct7[1]);
  not not_75 (not_75_out, funct7[2]);
  not not_76 (not_76_out, funct7[3]);
  not not_77 (not_77_out, funct7[4]);
  not not_78 (not_78_out, funct7[5]);
  not not_79 (not_79_out, funct7[6]);
  not not_80 (not_80_out, funct3[1]);
  not not_81 (not_81_out, funct7[0]);
  not not_82 (not_82_out, funct7[1]);
  not not_83 (not_83_out, funct7[2]);
  not not_84 (not_84_out, funct7[3]);
  not not_85 (not_85_out, funct7[4]);
  not not_86 (not_86_out, funct7[6]);
  not not_87 (not_87_out, funct3[0]);
  not not_88 (not_88_out, funct3[0]);
  not not_89 (not_89_out, funct3[1]);
  not not_90 (not_90_out, funct3[2]);
  not not_91 (not_91_out, funct7[1]);
  not not_92 (not_92_out, funct7[2]);
  not not_93 (not_93_out, funct7[3]);
  not not_94 (not_94_out, funct7[4]);
  not not_95 (not_95_out, funct7[5]);
  not not_96 (not_96_out, funct7[6]);
  not not_97 (not_97_out, funct3[1]);
  not not_98 (not_98_out, funct3[2]);
  not not_99 (not_99_out, funct7[0]);
  not not_100 (not_100_out, funct7[1]);
  not not_101 (not_101_out, funct7[2]);
  not not_102 (not_102_out, funct7[3]);
  not not_103 (not_103_out, funct7[4]);
  not not_104 (not_104_out, funct7[5]);
  not not_105 (not_105_out, funct7[6]);
  not not_106 (not_106_out, funct3[2]);
  not not_107 (not_107_out, funct7[1]);
  not not_108 (not_108_out, funct7[2]);
  not not_109 (not_109_out, funct7[3]);
  not not_110 (not_110_out, funct7[4]);
  not not_111 (not_111_out, funct7[5]);
  not not_112 (not_112_out, funct7[6]);
  not not_113 (not_113_out, funct3[0]);
  not not_114 (not_114_out, funct3[1]);
  not not_115 (not_115_out, funct7[0]);
  not not_116 (not_116_out, funct7[1]);
  not not_117 (not_117_out, funct7[2]);
  not not_118 (not_118_out, funct7[3]);
  not not_119 (not_119_out, funct7[4]);
  not not_120 (not_120_out, funct7[5]);
  not not_121 (not_121_out, funct7[6]);
  not not_122 (not_122_out, funct3[1]);
  not not_123 (not_123_out, funct7[0]);
  not not_124 (not_124_out, funct7[1]);
  not not_125 (not_125_out, funct7[2]);
  not not_126 (not_126_out, funct7[3]);
  not not_127 (not_127_out, funct7[4]);
  not not_128 (not_128_out, funct7[6]);
  not not_129 (not_129_out, funct7[0]);
  not not_130 (not_130_out, funct7[1]);
  not not_131 (not_131_out, funct7[2]);
  not not_132 (not_132_out, funct7[3]);
  not not_133 (not_133_out, funct7[4]);
  not not_134 (not_134_out, funct7[5]);
  not not_135 (not_135_out, funct7[6]);
  not not_136 (not_136_out, opcode[0]);
  not not_137 (not_137_out, opcode[1]);
  not not_138 (not_138_out, opcode[3]);
  not not_139 (not_139_out, opcode[4]);
  or or_6 (or_6_out, SLL0, SLLI);
  or or_7 (or_7_out, XOR0, XORI);
  or or_8 (or_8_out, OR0, ORI);
  Multiplexer #(.enable("false"), .width(4)) multiplexer_7 (.in0(4'b0000), .in1(4'b1010), .out(MUL_GROUP), .sel(MUL));
  Multiplexer #(.enable("false"), .width(4)) multiplexer_8 (
    .in0(4'b0000), .in1(4'b0110), .out(SLL_GROUP), .sel(or_6_out));
  Multiplexer #(.enable("false"), .width(4)) multiplexer_9 (
    .in0(4'b0000), .in1(4'b1011), .out(MULHU_GROUP), .sel(MULHU));
  Multiplexer #(.enable("false"), .width(4)) multiplexer_10 (
    .in0(4'b0000), .in1(4'b0011), .out(XOR_GROUP), .sel(or_7_out));
  Multiplexer #(.enable("false"), .width(4)) multiplexer_11 (
    .in0(4'b0000), .in1(4'b0010), .out(OR_GROUP), .sel(or_8_out));
  and and_13 (SRLI, funct3[0], not_72_out, funct3[2], not_73_out, not_74_out, not_75_out, not_76_out, not_77_out, not_78_out, not_79_out, I);
  and and_14 (SRAI, funct3[0], not_80_out, funct3[2], not_81_out, not_82_out, not_83_out, not_84_out, not_85_out, funct7[5], not_86_out, I);
  and and_15 (ORI, not_87_out, funct3[1], funct3[2], I);
  and and_16 (MUL, not_88_out, not_89_out, not_90_out, funct7[0], not_91_out, not_92_out, not_93_out, not_94_out, not_95_out, not_96_out, R);
  and and_17 (SLL0, funct3[0], not_97_out, not_98_out, not_99_out, not_100_out, not_101_out, not_102_out, not_103_out, not_104_out, not_105_out, R);
  and and_18 (MULHU, funct3[0], funct3[1], not_106_out, funct7[0], not_107_out, not_108_out, not_109_out, not_110_out, not_111_out, not_112_out, R);
  and and_19 (XOR0, not_113_out, not_114_out, funct3[2], not_115_out, not_116_out, not_117_out, not_118_out, not_119_out, not_120_out, not_121_out, R);
  and and_20 (SRA0, funct3[0], not_122_out, funct3[2], not_123_out, not_124_out, not_125_out, not_126_out, not_127_out, funct7[5], not_128_out, R);
  and and_21 (AND0, funct3[0], funct3[1], funct3[2], not_129_out, not_130_out, not_131_out, not_132_out, not_133_out, not_134_out, not_135_out, R);
  Multiplexer #(.enable("false"), .width(4)) multiplexer_12 (
    .in0(4'b0000), .in1(4'b0100), .out(SRL_GROUP), .sel(or_9_out));
  or or_9 (or_9_out, SRL0, SRLI);
  and and_22 (I, not_136_out, not_137_out, opcode[2], not_138_out, not_139_out);

  // Other names for the same wires on the sheet: B0 = funct3[0]; B1 = funct3[1]; B2 = funct3[2]; C0 = funct7[0];
  //   C1 = funct7[1]; C2 = funct7[2]; C3 = funct7[3]; C4 = funct7[4]; C5 = funct7[5]; C6 = funct7[6]; A0 = opcode[0];
  //   A1 = opcode[1]; A2 = opcode[2]; A3 = opcode[3]; A4 = opcode[4]
endmodule

module WBSel0 (
  input  [4:0] opcode,
  input  [6:0] funct7,
  input  [2:0] funct3,
  output [1:0] WBSel_Output
);

  wire I, I_JALR, not_1_out, not_2_out, not_3_out, not_4_out, not_5_out, not_6_out, not_7_out, not_8_out,
       not_9_out, not_10_out, not_11_out, not_12_out, not_13_out, not_14_out, not_15_out, not_16_out,
       not_17_out, not_18_out, or_1_out, or_3_out, R, U_AUIPC, U_LUI, UJ;
  wire [1:0] GROUP1, GROUP2;

  not not_1 (not_1_out, opcode[0]);
  not not_2 (not_2_out, opcode[1]);
  not not_3 (not_3_out, opcode[4]);
  not not_4 (not_4_out, opcode[1]);
  not not_5 (not_5_out, opcode[3]);
  not not_6 (not_6_out, opcode[4]);
  not not_7 (not_7_out, opcode[1]);
  not not_8 (not_8_out, opcode[2]);
  not not_9 (not_9_out, funct3[0]);
  not not_10 (not_10_out, funct3[1]);
  not not_11 (not_11_out, funct3[2]);
  and and_1 (R, not_1_out, not_2_out, opcode[2], opcode[3], not_3_out);
  and and_2 (U_AUIPC, opcode[0], not_4_out, opcode[2], not_5_out, not_6_out);
  and and_3 (I_JALR, opcode[0], not_7_out, not_8_out, opcode[3], opcode[4], not_9_out, not_10_out, not_11_out);
  or or_1 (or_1_out, R, I, U_AUIPC, U_LUI);
  assign WBSel_Output = GROUP1 | GROUP2;  // OR_Gate or_2, 2 bits wide
  Multiplexer #(.enable("false"), .width(2)) multiplexer_1 (.in0(2'b00), .in1(2'b01), .out(GROUP1), .sel(or_1_out));
  not not_12 (not_12_out, opcode[1]);
  not not_13 (not_13_out, opcode[4]);
  not not_14 (not_14_out, opcode[2]);
  not not_15 (not_15_out, opcode[0]);
  not not_16 (not_16_out, opcode[1]);
  not not_17 (not_17_out, opcode[3]);
  not not_18 (not_18_out, opcode[4]);
  or or_3 (or_3_out, I_JALR, UJ);
  and and_4 (U_LUI, opcode[0], not_12_out, opcode[2], opcode[3], not_13_out);
  and and_5 (UJ, opcode[0], opcode[1], not_14_out, opcode[3], opcode[4]);
  Multiplexer #(.enable("false"), .width(2)) multiplexer_2 (.in0(2'b00), .in1(2'b10), .out(GROUP2), .sel(or_3_out));
  and and_6 (I, not_15_out, not_16_out, opcode[2], not_17_out, not_18_out);

  // Other names for the same wires on the sheet: B0 = funct3[0]; B1 = funct3[1]; B2 = funct3[2]; C0 = funct7[0];
  //   C1 = funct7[1]; C2 = funct7[2]; C3 = funct7[3]; C4 = funct7[4]; C5 = funct7[5]; C6 = funct7[6]; A0 = opcode[0];
  //   A1 = opcode[1]; A2 = opcode[2]; A3 = opcode[3]; A4 = opcode[4]
endmodule

module ImmSel0 (
  input  [4:0] opcode,
  input  [6:0] funct7,
  input  [2:0] funct3,
  output [2:0] ImmSel_Output
);

  wire not_1_out, not_2_out, not_3_out, not_4_out, not_5_out, not_6_out, not_7_out, not_8_out, not_9_out,
       not_10_out, not_11_out, not_12_out, not_13_out, or_1_out, S, SB, U_AUIPC, U_LUI, UJ;
  wire [2:0] GROUP1, GROUP2, GROUP3, GROUP4;

  not not_1 (not_1_out, opcode[1]);
  not not_2 (not_2_out, opcode[3]);
  not not_3 (not_3_out, opcode[4]);
  not not_4 (not_4_out, opcode[0]);
  not not_5 (not_5_out, opcode[1]);
  not not_6 (not_6_out, opcode[2]);
  not not_7 (not_7_out, opcode[2]);
  Multiplexer #(.enable("false"), .width(3)) multiplexer_1 (.in0(3'b000), .in1(3'b001), .out(GROUP1), .sel(S));
  or or_1 (or_1_out, U_AUIPC, U_LUI);
  Multiplexer #(.enable("false"), .width(3)) multiplexer_2 (.in0(3'b000), .in1(3'b011), .out(GROUP3), .sel(or_1_out));
  and and_1 (U_AUIPC, opcode[0], not_1_out, opcode[2], not_2_out, not_3_out);
  and and_2 (SB, not_4_out, not_5_out, not_6_out, opcode[3], opcode[4]);
  and and_3 (UJ, opcode[0], opcode[1], not_7_out, opcode[3], opcode[4]);
  assign ImmSel_Output = GROUP1 | GROUP2 | GROUP3 | GROUP4;  // OR_Gate or_2, 3 bits wide
  not not_8 (not_8_out, opcode[1]);
  not not_9 (not_9_out, opcode[4]);
  not not_10 (not_10_out, opcode[0]);
  not not_11 (not_11_out, opcode[1]);
  not not_12 (not_12_out, opcode[2]);
  not not_13 (not_13_out, opcode[4]);
  Multiplexer #(.enable("false"), .width(3)) multiplexer_3 (.in0(3'b000), .in1(3'b010), .out(GROUP2), .sel(SB));
  Multiplexer #(.enable("false"), .width(3)) multiplexer_4 (.in0(3'b000), .in1(3'b100), .out(GROUP4), .sel(UJ));
  and and_4 (U_LUI, opcode[0], not_8_out, opcode[2], opcode[3], not_9_out);
  and and_5 (S, not_10_out, not_11_out, not_12_out, opcode[3], not_13_out);

  // Other names for the same wires on the sheet: B0 = funct3[0]; B1 = funct3[1]; B2 = funct3[2]; C0 = funct7[0];
  //   C1 = funct7[1]; C2 = funct7[2]; C3 = funct7[3]; C4 = funct7[4]; C5 = funct7[5]; C6 = funct7[6]; A0 = opcode[0];
  //   A1 = opcode[1]; A2 = opcode[2]; A3 = opcode[3]; A4 = opcode[4]
endmodule
