// Logisim project cpu.circ as structural Verilog: 4 circuits, main circuit cpu
module cpu (
  input  clk,
  input  [31:0] INSTRUCTION,
  input  [31:0] READ_DATA,
  output [31:0] WRITE_ADDRESS,
  output [31:0] PROGRAM_COUNTER,
  output [31:0] ra,
  output [31:0] sp,
  output [31:0] t0,
  output [31:0] t1,
  output [31:0] t2,
  output [31:0] s0,
  output [31:0] s1,
  output [31:0] a0,
  output [31:0] tohost,
  output [3:0] WRITE_ENABLE,
  output [31:0] WRITE_DATA
);

  wire ASel, BrEq, BrLt, BrUn, BSel, CSRSel, CSRWen, MemRW, PCSel, RegWEn;
  wire [1:0] WBSel;
  wire [2:0] ImmSel;
  wire [3:0] ALUSel, LOAD_ENABLE;
  wire [4:0] rd, rs1, rs2;
  wire [31:0] A, adder_1_out, adder_2_out, B, imm, INSTRUCTION_EX, INSTRUCTION_PCSel, multiplexer_1_out,
       PROGRAM_COUNTER_EX, read_data_1, READ_DATA_MASKED, WRITE_BACK;

  // Probe on PCSel
  Multiplexer #(.enable("false"), .width(32)) multiplexer_1 (
    .in0(adder_1_out), .in1(WRITE_ADDRESS), .out(multiplexer_1_out), .sel(PCSel));
  // Probe on PROGRAM_COUNTER_EX
  // Probe on INSTRUCTION_EX
  Adder #(.width(32)) adder_1 (.a(PROGRAM_COUNTER), .b(32'h4), .out(adder_1_out));  // open: cin, cout
  Register #(.width(32)) PC (.D(multiplexer_1_out), .clk(clk), .Q(PROGRAM_COUNTER));  // open: en, clr
  // control_logic control_logic_1: pin names not known; wires that end beside it: INSTRUCTION_EX, BrEq, BrLt, PCSel, RegWEn, ImmSel, BrUn, ASel, BSel, ALUSel, MemRW, WBSel, CSRSel, CSRWen, WRITE_ENABLE
  decode decode_1 (.INST(INSTRUCTION_EX), .RD(rd), .RS1(rs1), .RS2(rs2));
  // Probe on rs1
  // Probe on rs2
  // Probe on rd
  // Probe on read_data_1
  regfile regfile_1 (
    .rs1(rs1), .rs2(rs2), .rd(rd), .Write_Data(WRITE_BACK), .RegWEn(RegWEn), .clk(clk), .ra(ra), .sp(sp),
    .t0(t0), .t1(t1), .t2(t2), .s0(s0), .s1(s1), .a0(a0), .Read_Data_1(read_data_1), .Read_Data_2(WRITE_DATA));
  // Probe on WRITE_DATA
  branch_comp branch_comp_1 (.rs1(read_data_1), .rs2(WRITE_DATA), .BrUn(BrUn), .BrEq(BrEq), .BrLt(BrLt));
  Multiplexer #(.enable("false"), .width(32)) multiplexer_2 (
    .in0(INSTRUCTION), .in1(32'h13), .out(INSTRUCTION_PCSel), .sel(PCSel));
  // Probe on imm
  // Probe on A
  // Probe on B
  imm_gen imm_gen_1 (.inst(INSTRUCTION_EX), .ImmSel(ImmSel), .imm(imm));
  IF_EX if_ex_1 (
    .Clock(clk), .PC_IN(PROGRAM_COUNTER), .INST_IN(INSTRUCTION_PCSel), .PC_OUT(PROGRAM_COUNTER_EX),
    .INST_OUT(INSTRUCTION_EX));
  // Probe on read_data_1
  // Probe on ASel
  // Probe on WRITE_DATA
  // Probe on BSel
  // Probe on INSTRUCTION_EX
  Multiplexer #(.enable("false"), .width(32)) multiplexer_3 (
    .in0(read_data_1), .in1(PROGRAM_COUNTER_EX), .out(A), .sel(ASel));
  Multiplexer #(.enable("false"), .width(32)) multiplexer_4 (.in0(WRITE_DATA), .in1(imm), .out(B), .sel(BSel));
  alu alu_1 (.Result(WRITE_ADDRESS), .A(A), .B(B), .ALUSel(ALUSel));
  // Probe on WRITE_ADDRESS
  Adder #(.width(32)) adder_2 (.a(PROGRAM_COUNTER_EX), .b(32'h4), .out(adder_2_out));  // open: cin, cout
  // Probe on LOAD_ENABLE
  Multiplexer #(.enable("false"), .select(2), .width(32)) multiplexer_5 (
    .in0(READ_DATA_MASKED), .in1(WRITE_ADDRESS), .in2(adder_2_out), .out(WRITE_BACK), .sel(WBSel));  // open: in3
  // Probe on WRITE_BACK
  // Probe on WBSel
  // Probe on READ_DATA_MASKED
  read_mask read_mask_1 (.READ_ENABLE(LOAD_ENABLE), .READ_DATA(READ_DATA), .READ_MASK_OUTPUT(READ_DATA_MASKED));
  csr csr_1 (.clk(clk), .tohost(tohost));  // open: CSR_address, CSR_din, CSR_WE
  // also tied to GND on the sheet: {tohost[0], tohost[1], tohost[2], tohost[3], tohost[4], tohost[5], tohost[6], tohost[7], tohost[8], tohost[9], tohost[10], tohost[11], tohost[12], tohost[13], tohost[14], tohost[15], tohost[16], tohost[17], tohost[18], tohost[19], tohost[20], tohost[21], tohost[22], tohost[23], tohost[24], tohost[25], tohost[26], tohost[27], tohost[28], tohost[29], tohost[30], tohost[31]}

  // Other names for the same wires on the sheet: alu_result[31:0] = WRITE_ADDRESS; read_data_2[31:0] = WRITE_DATA

  // Notes on the sheet:
  //   Output to IMEM
  //   IMEM (do **NOT** move this)
  //   Inputs from IMEM
  //   It is OK to move the PC, RegFile, ALU, MEM, Branch Comp, Imm Gen, and Control Logic to wherever is most convenient for you when constructing your CPU, and to delete this text
  //   Inputs/Outputs for testing. Do **NOT** move these.
  //   Outputs To DMEM
  //   DMEM (do **NOT** move this)
  //   Inputs From DMEM
endmodule

module decode (
  input  [31:0] INST,
  output [4:0] RD,
  output [4:0] RS1,
  output [4:0] RS2
);


  assign RD = INST[11:7];
  assign RS1 = INST[19:15];
  assign RS2 = INST[24:20];
endmodule

module IF_EX (
  input  Clock,
  input  [31:0] PC_IN,
  input  [31:0] INST_IN,
  output [31:0] PC_OUT,
  output [31:0] INST_OUT
);

  Register #(.width(32)) register_1 (.D(PC_IN), .clk(Clock), .Q(PC_OUT));  // open: en, clr
  Register #(.width(32)) register_2 (.D(INST_IN), .clk(Clock), .Q(INST_OUT));  // open: en, clr

  // Other names for the same wires on the sheet: CLK = Clock
endmodule

module read_mask (
  input  [3:0] READ_ENABLE,
  input  [31:0] READ_DATA,
  output [31:0] READ_MASK_OUTPUT
);

  wire [31:0] Byte, HalfWord;

  assign Byte = {{24{READ_DATA[7]}}, READ_DATA[7:0]};  // Bit_Extender bit_extender_1
  assign HalfWord = {{16{READ_DATA[15]}}, READ_DATA[15:0]};  // Bit_Extender bit_extender_2
  Multiplexer #(.enable("false"), .select(4), .width(32)) multiplexer_1 (
    .in0({32{1'b0}}), .in1(Byte), .in3(HalfWord), .in15(READ_DATA), .out(READ_MASK_OUTPUT), .sel(READ_ENABLE));  // open: in2, in4, in5, in6, in7, in8, in9, in10, in11, in12, in13, in14

  // Other names for the same wires on the sheet: Byte1[7:0] = READ_DATA[7:0]; Word[31:0] = READ_DATA;
  //   Byte2[7:0] = READ_DATA[15:8]; Byte3[7:0] = READ_DATA[23:16]; Byte4[7:0] = READ_DATA[31:24]
endmodule
