// Logisim project imm_gen.circ as structural Verilog: 6 circuits, main circuit imm_gen
module imm_gen (
  input  [31:0] inst,
  input  [2:0] ImmSel,
  output [31:0] imm
);

  wire [31:0] i_imm_1_imm, s_imm_1_imm, sb_imm_1_imm, u_imm_1_imm, uj_imm_1_imm;

  I_imm i_imm_1 (.INST(inst), .IMM(i_imm_1_imm));
  S_imm s_imm_1 (.INST(inst), .IMM(s_imm_1_imm));
  SB_imm sb_imm_1 (.INST(inst), .IMM(sb_imm_1_imm));
  U_imm u_imm_1 (.INST(inst), .IMM(u_imm_1_imm));
  UJ_imm uj_imm_1 (.INST(inst), .IMM(uj_imm_1_imm));
  Multiplexer #(.enable("false"), .select(3), .width(32)) multiplexer_1 (
    .in0(i_imm_1_imm), .in1(s_imm_1_imm), .in2(sb_imm_1_imm), .in3(u_imm_1_imm), .in4(uj_imm_1_imm),
    .out(imm), .sel(ImmSel));  // open: in5, in6, in7

  // Notes on the sheet:
  //   INPUTS to your circuit
  //   DON'T CHANGE THE LOCATIONS OF THE INPUTS AND OUTPUTS!
  //   OUTPUT from your circuit
endmodule

module I_imm (
  input  [31:0] INST,
  output [31:0] IMM
);

  assign IMM = {{21{INST[31]}}, INST[30:20]};  // Bit_Extender bit_extender_1
endmodule

module S_imm (
  input  [31:0] INST,
  output [31:0] IMM
);

  assign IMM = {{21{INST[31]}}, {INST[30:25], INST[11:7]}};  // Bit_Extender bit_extender_1
endmodule

module SB_imm (
  input  [31:0] INST,
  output [31:0] IMM
);

  assign IMM = {{20{INST[31]}}, {INST[7], INST[30:25], INST[11:8], 1'b0}};  // Bit_Extender bit_extender_1
endmodule

module U_imm (
  input  [31:0] INST,
  output [31:0] IMM
);


  assign IMM = {INST[31:12], {12{1'b0}}};
endmodule

module UJ_imm (
  input  [31:0] INST,
  output [31:0] IMM
);

  assign IMM = {{12{INST[31]}}, {INST[19:12], INST[20], INST[30:21], 1'b0}};  // Bit_Extender bit_extender_1
endmodule
