// Logisim project regfile.circ as structural Verilog: 2 circuits, main circuit regfile
module regfile (
  input  [4:0] rs1,
  input  [4:0] rs2,
  input  [4:0] rd,
  input  [31:0] Write_Data,
  input  RegWEn,
  input  clk,
  output [31:0] ra,
  output [31:0] sp,
  output [31:0] t0,
  output [31:0] t1,
  output [31:0] t2,
  output [31:0] s0,
  output [31:0] s1,
  output [31:0] a0,
  output [31:0] Read_Data_1,
  output [31:0] Read_Data_2
);

  wire demultiplexer_1_out0, write_en1, write_en2, write_en3, write_en4, write_en5, write_en6, write_en7,
       write_en8, write_en9, write_en10, write_en11, write_en12, write_en13, write_en14, write_en15,
       write_en16, write_en17, write_en18, write_en19, write_en20, write_en21, write_en22, write_en23,
       write_en24, write_en25, write_en26, write_en27, write_en28, write_en29, write_en30, write_en31;
  wire [31:0] x0, x3, x4, x11, x12, x13, x14, x15, x16, x17, x18, x19, x20, x21, x22, x23, x24, x25, x26,
       x27, x28, x29, x30, x31;

  reg0 reg0_1 (.WriteData(Write_Data), .WE(1'b0), .CLK(clk), .StateVal(x0));
  reg0 reg0_2 (.WriteData(Write_Data), .WE(write_en1), .CLK(clk), .StateVal(ra));
  reg0 reg0_3 (.WriteData(Write_Data), .WE(write_en2), .CLK(clk), .StateVal(sp));
  reg0 reg0_4 (.WriteData(Write_Data), .WE(write_en3), .CLK(clk), .StateVal(x3));
  reg0 reg0_5 (.WriteData(Write_Data), .WE(write_en4), .CLK(clk), .StateVal(x4));
  reg0 reg0_6 (.WriteData(Write_Data), .WE(write_en5), .CLK(clk), .StateVal(t0));
  reg0 reg0_7 (.WriteData(Write_Data), .WE(write_en6), .CLK(clk), .StateVal(t1));
  reg0 reg0_8 (.WriteData(Write_Data), .WE(write_en7), .CLK(clk), .StateVal(t2));
  Multiplexer #(.enable("false"), .select(5), .width(32)) multiplexer_1 (
    .in0(x0), .in1(ra), .in2(sp), .in3(x3), .in4(x4), .in5(t0), .in6(t1), .in7(t2), .in8(s0), .in9(s1),
    .in10(a0), .in11(x11), .in12(x12), .in13(x13), .in14(x14), .in15(x15), .in16(x16), .in17(x17),
    .in18(x18), .in19(x19), .in20(x20), .in21(x21), .in22(x22), .in23(x23), .in24(x24), .in25(x25),
    .in26(x26), .in27(x27), .in28(x28), .in29(x29), .in30(x30), .in31(x31), .out(Read_Data_1), .sel(rs1));
  Multiplexer #(.enable("false"), .select(5), .width(32)) multiplexer_2 (
    .in0(x0), .in1(ra), .in2(sp), .in3(x3), .in4(x4), .in5(t0), .in6(t1), .in7(t2), .in8(s0), .in9(s1),
    .in10(a0), .in11(x11), .in12(x12), .in13(x13), .in14(x14), .in15(x15), .in16(x16), .in17(x17),
    .in18(x18), .in19(x19), .in20(x20), .in21(x21), .in22(x22), .in23(x23), .in24(x24), .in25(x25),
    .in26(x26), .in27(x27), .in28(x28), .in29(x29), .in30(x30), .in31(x31), .out(Read_Data_2), .sel(rs2));
  reg0 reg0_9 (.WriteData(Write_Data), .WE(write_en8), .CLK(clk), .StateVal(s0));
  reg0 reg0_10 (.WriteData(Write_Data), .WE(write_en9), .CLK(clk), .StateVal(s1));
  reg0 reg0_11 (.WriteData(Write_Data), .WE(write_en10), .CLK(clk), .StateVal(a0));
  reg0 reg0_12 (.WriteData(Write_Data), .WE(write_en11), .CLK(clk), .StateVal(x11));
  reg0 reg0_13 (.WriteData(Write_Data), .WE(write_en12), .CLK(clk), .StateVal(x12));
  reg0 reg0_14 (.WriteData(Write_Data), .WE(write_en13), .CLK(clk), .StateVal(x13));
  reg0 reg0_15 (.WriteData(Write_Data), .WE(write_en14), .CLK(clk), .StateVal(x14));
  reg0 reg0_16 (.WriteData(Write_Data), .WE(write_en15), .CLK(clk), .StateVal(x15));
  Demultiplexer #(.enable("false"), .select(5)) demultiplexer_1 (
    .out0(demultiplexer_1_out0), .out1(write_en1), .out2(write_en2), .out3(write_en3), .out4(write_en4),
    .out5(write_en5), .out6(write_en6), .out7(write_en7), .out8(write_en8), .out9(write_en9),
    .out10(write_en10), .out11(write_en11), .out12(write_en12), .out13(write_en13), .out14(write_en14),
    .out15(write_en15), .out16(write_en16), .out17(write_en17), .out18(write_en18), .out19(write_en19),
    .out20(write_en20), .out21(write_en21), .out22(write_en22), .out23(write_en23), .out24(write_en24),
    .out25(write_en25), .out26(write_en26), .out27(write_en27), .out28(write_en28), .out29(write_en29),
    .out30(write_en30), .out31(write_en31), .in(RegWEn), .sel(rd));
  reg0 reg0_17 (.WriteData(Write_Data), .WE(write_en16), .CLK(clk), .StateVal(x16));
  reg0 reg0_18 (.WriteData(Write_Data), .WE(write_en17), .CLK(clk), .StateVal(x17));
  reg0 reg0_19 (.WriteData(Write_Data), .WE(write_en18), .CLK(clk), .StateVal(x18));
  reg0 reg0_20 (.WriteData(Write_Data), .WE(write_en19), .CLK(clk), .StateVal(x19));
  reg0 reg0_21 (.WriteData(Write_Data), .WE(write_en20), .CLK(clk), .StateVal(x20));
  reg0 reg0_22 (.WriteData(Write_Data), .WE(write_en21), .CLK(clk), .StateVal(x21));
  reg0 reg0_23 (.WriteData(Write_Data), .WE(write_en22), .CLK(clk), .StateVal(x22));
  reg0 reg0_24 (.WriteData(Write_Data), .WE(write_en23), .CLK(clk), .StateVal(x23));
  // Probe on demultiplexer_1_out0
  reg0 reg0_25 (.WriteData(Write_Data), .WE(write_en24), .CLK(clk), .StateVal(x24));
  reg0 reg0_26 (.WriteData(Write_Data), .WE(write_en25), .CLK(clk), .StateVal(x25));
  reg0 reg0_27 (.WriteData(Write_Data), .WE(write_en26), .CLK(clk), .StateVal(x26));
  reg0 reg0_28 (.WriteData(Write_Data), .WE(write_en27), .CLK(clk), .StateVal(x27));
  reg0 reg0_29 (.WriteData(Write_Data), .WE(write_en28), .CLK(clk), .StateVal(x28));
  reg0 reg0_30 (.WriteData(Write_Data), .WE(write_en29), .CLK(clk), .StateVal(x29));
  reg0 reg0_31 (.WriteData(Write_Data), .WE(write_en30), .CLK(clk), .StateVal(x30));
  reg0 reg0_32 (.WriteData(Write_Data), .WE(write_en31), .CLK(clk), .StateVal(x31));

  // Other names for the same wires on the sheet: read_data1[31:0] = Read_Data_1; read_data2[31:0] = Read_Data_2;
  //   read_reg1[4:0] = rs1; read_reg2[4:0] = rs2; write_en = RegWEn; write_reg[4:0] = rd; x1[31:0] = ra;
  //   x2[31:0] = sp; x5[31:0] = t0; x6[31:0] = t1; x7[31:0] = t2; x8[31:0] = s0; x9[31:0] = s1; x10[31:0] = a0

  // Notes on the sheet:
  //   INPUTS to your circuit
  //   DON'T CHANGE THE LOCATIONS OF THE INPUTS AND OUTPUTS!
  //   These are DEBUG/TEST outputs from your circuit.
  //   OUTPUTS from your circuit
endmodule

module reg0 (
  input  [31:0] WriteData,
  input  WE,
  input  CLK,
  output [31:0] StateVal
);

  Register #(.width(32)) register_1 (.D(WriteData), .en(WE), .clk(CLK), .Q(StateVal));  // open: clr
endmodule
